# Fritzing sketch Schematics (saved by Fritzing 0.9.6b)

parts:
  MCU1 = Raspberry Pi Zero
  Part1 = PowerBoost 500 Charger
  U1 = LIPO-1000mAh [package=lipo-1000]
  J1 = Basic Servo
  U2 = LIPO-2000mAh [package=lipo-2000]
  M1 = RioRand LM2596
  IC2 = IC, DIP package, 8 pins [chip_label=ESC]
  M2 = DC Motor
  IC3 = IC, DIP package, 12 pins [chip_label="RC Rcvr"]
  Part2 = I2C level shifter bidirectional

nets:
  N1: MCU1.pin_1, MCU1.pin_17, Part2.LV
  N2: MCU1.pin_6, MCU1.pin_9, MCU1.pin_34, IC3.pin3, Part2.GND
  N3: MCU1.pin_7, IC3.pin4
  N4: MCU1.pin_11, Part2.LV1
  N5: MCU1.pin_13, Part2.LV2
  N6: MCU1.pin_32, IC2.pin6
  N7: MCU1.pin_33, J1.pulse
  N8: Part1.GND_BAT_IN, U1.-
  N9: Part1.VBAT_IN, U1.+
  N10: Part1.USB, Part2.HV2
  N11: J1.gnd, IC2.pin8
  N12: J1.vcc, IC2.pin7
  N13: U2.+, M1.Pin_1, IC2.pin1
  N14: U2.-, M1.Pin_2, IC2.pin2
  N15: IC2.pin3, M2.pin_1
  N16: IC2.pin4, M2.pin_2
  N17: IC3.pin1, Part2.HV1
  N18: IC3.pin2, Part2.HV

notes:
  11.1V LiPo Battery
  Check
  - Powerboost
  - 3V3 as signal
